// Logisim project cpu.circ as structural Verilog: 2 circuits, main circuit main
module main (
  input  [31:0] RS_READ_VALUE,
  input  [31:0] RT_READ_VALUE,
  input  [31:0] INSTRUCTION,
  input  CLOCK,
  input  RESET,
  output [31:0] t0,
  output [31:0] t1,
  output [31:0] t2,
  output [31:0] t3,
  output [4:0] RS,
  output [4:0] RT,
  output [4:0] Write_Register,
  output [31:0] RD_WRITE_VALUE,
  output RD_WRITE_ENABLE,
  output [23:0] FETCH_ADDRESS
);

  wire ALUSrc, Branch, equal, Jump, MemRead, MemtoReg, MemWrite, overflow, RegDst;
  wire [5:0] funct;
  wire [23:0] adder_1_out, multiplexer_4_out;
  wire [31:0] ALU_result, bit_extender_2_out, MEM_data_mem_out, multiplexer_2_out;

  Multiplexer #(.width(5), .enable("false")) multiplexer_1 (
    .in0(INSTRUCTION[20:16]), .in1(INSTRUCTION[15:11]), .out(Write_Register), .sel(RegDst));
  Bit_Extender #(.in_width(16), .out_width(6)) bit_extender_1 (.in(INSTRUCTION[15:0]), .out(funct));
  Multiplexer #(.width(32), .enable("false")) multiplexer_2 (
    .in0(RT_READ_VALUE), .in1(bit_extender_2_out), .out(multiplexer_2_out), .sel(ALUSrc));
  assign bit_extender_2_out = {{16{1'b0}}, INSTRUCTION[15:0]};  // Bit_Extender bit_extender_2
  alu_main ALU (
    .Switch__S(funct), .X(RS_READ_VALUE), .Equal(equal), .RESULT(ALU_result), .Signed_Overflow(overflow),
    .Y(multiplexer_2_out));
  Register #(.width(24)) register_1 (.D(multiplexer_4_out), .Q(FETCH_ADDRESS));  // open: en, clk, clr
  mem_main MEM (
    .Data_Mem_Addr(ALU_result), .Data_Mem_In(RT_READ_VALUE), .MEM_WRITE(MemWrite), .CLOCK(CLOCK),
    .Data_Mem_Out(MEM_data_mem_out));  // open: ACCESS_BYTE
  // regfile_main RegFile: pin names not known
  Multiplexer #(.width(32), .enable("false")) multiplexer_3 (
    .in0(ALU_result), .in1(MEM_data_mem_out), .out(RD_WRITE_VALUE), .sel(MemtoReg));
  Adder #(.width(24)) adder_1 (.a(FETCH_ADDRESS), .b(24'h1), .out(adder_1_out));  // open: cin, cout
  Multiplexer #(.width(24), .enable("false")) multiplexer_4 (
    .in0(adder_1_out), .out(multiplexer_4_out), .sel(Branch));  // open: in1
  ControlUnit controlunit_1 (
    .opcode(INSTRUCTION[31:26]), .RegDst(RegDst), .Branch(Branch), .MemRead(MemRead), .MemToReg(MemtoReg),
    .MemWrite(MemWrite), .ALUSrc(ALUSrc), .RegWrite(RD_WRITE_ENABLE), .Jump(Jump));

  assign RS = INSTRUCTION[25:21];
  assign RT = INSTRUCTION[20:16];

  // Other names for the same wires on the sheet: CLK = CLOCK; immdt[15:0] = INSTRUCTION[15:0];
  //   instRD[4:0] = INSTRUCTION[15:11]; instRT[4:0] = INSTRUCTION[20:16]; instRS[4:0] = INSTRUCTION[25:21];
  //   opcode[5:0] = INSTRUCTION[31:26]; memData[31:0] = RD_WRITE_VALUE; PC[23:0] = FETCH_ADDRESS;
  //   RegWrite = RD_WRITE_ENABLE; rsData[31:0] = RS_READ_VALUE; rtData[31:0] = RT_READ_VALUE

  // Notes on the sheet:
  //   These are outputs/inputs from run.circ
  //   These are outputs to run.circ
  //   Feel free to move these components
endmodule

module ControlUnit (
  input  [5:0] opcode,
  output RegDst,
  output Branch,
  output MemRead,
  output MemToReg,
  output MemWrite,
  output ALUSrc,
  output RegWrite,
  output Jump
);

  wire and_7_out;

  and and_1 (RegDst, ~opcode[5], ~opcode[4], ~opcode[3], ~opcode[2], ~opcode[1], ~opcode[0]);  // AND_Gate
  and and_2 (Jump, ~opcode[5], ~opcode[4], ~opcode[3], ~opcode[2], opcode[1]);  // AND_Gate
  and and_3 (Branch, ~opcode[5], ~opcode[4], ~opcode[3], opcode[2], ~opcode[1]);  // AND_Gate
  and and_4 (MemRead, opcode[5], ~opcode[3]);  // AND_Gate
  and and_5 (ALUSrc, ~RegDst, ~Branch);  // AND_Gate
  and and_6 (MemWrite, opcode[5], ~opcode[4], opcode[3], ~opcode[2], opcode[1], opcode[0]);  // AND_Gate
  and and_7 (and_7_out, ~MemWrite, ~Branch, ~Jump);  // AND_Gate
  or or_1 (RegWrite, RegDst, and_7_out);

  assign MemToReg = MemRead;
endmodule
